# Fritzing sketch ProjetoSysResultado (saved by Fritzing 0.9.3b)
breadboards: 1

parts:
  UNOR3 = Arduino Uno (Rev3)
  LED1 = smd LED [color="Red (633nm)" package="0603 [SMD]"]
  R1 = Resistor [tolerance=±5% resistance=100 package="0805 [SMD]"]
  S1 = Pushbutton [package="[THT]"]
  R2 = Resistor [tolerance=±5% resistance=150 package="0805 [SMD]"]

nets:
  N1: UNOR3.D8, R1.Pin_0
  N2: UNOR3.D2, UNOR3.5V, S1.Pin_1, S1.Pin_2, S1.Pin_3, S1.Pin_4, R2.Pin_1
  N3: UNOR3.GND, R2.Pin_0
  N4: LED1.anode, R1.Pin_1
